# Fritzing sketch thermal_printer_rpi (saved by Fritzing 0.9.3b)

parts:
  Raspberry_Pi_1 = Raspberry Pi 3 [part_number=RPI-3-V1.2]  # not connected
  Part1 = Thermal Printer
  JACK1 = 2.1mm Barrel Jack with Terminal Block

nets:
  N1: Part1.VH, JACK1.POS
